// Logisim project fib manual.circ as structural Verilog: 1 circuit, main circuit main
module main (
);

  wire button_1_out, button_2_out, button_3_out, pull_resistor_1_node, pull_resistor_2_node,
       pull_resistor_3_node, s_r_ff_1_q, s_r_ff_1_qn;
  wire [31:0] A_q, adder_1_out, B_q, C_q, controlled_buffer_1_out;

  Pull_Resistor pull_resistor_1 (.node(pull_resistor_1_node));
  Pull_Resistor pull_resistor_2 (.node(pull_resistor_2_node));
  Pull_Resistor pull_resistor_3 (.node(pull_resistor_3_node));
  Button button_1 (.out(button_1_out));
  Button button_2 (.out(button_2_out));
  Button button_3 (.out(button_3_out));
  Button button_4 (.out(pull_resistor_2_node));
  Button button_5 (.out(pull_resistor_1_node));
  Button button_6 (.out(pull_resistor_3_node));
  Pull_Resistor pull_resistor_4 (.node(button_1_out));
  Pull_Resistor pull_resistor_5 (.node(button_3_out));
  Pull_Resistor pull_resistor_6 (.node(button_2_out));
  S_R_Flip_Flop s_r_ff_1 (
    .Q(s_r_ff_1_q), .Qn(s_r_ff_1_qn), .preset(pull_resistor_1_node), .reset(pull_resistor_3_node));  // open: S, clk, R, en
  assign controlled_buffer_1_out = s_r_ff_1_qn ? 32'h1 : 32'bz;  // Controlled_Buffer controlled_buffer_1
  assign controlled_buffer_1_out = s_r_ff_1_q ? C_q : 32'bz;  // Controlled_Buffer controlled_buffer_2
  // Probe on A_q
  Register #(.width(32)) A (.D(B_q), .Q(A_q), .clk(button_2_out), .clr(button_1_out));  // open: en
  Register #(.width(32)) B (.D(controlled_buffer_1_out), .Q(B_q), .clk(button_3_out));  // open: en, clr
  Register #(.width(32)) C (.D(adder_1_out), .Q(C_q), .clk(pull_resistor_2_node));  // open: en, clr
  Adder #(.width(32)) adder_1 (.a(A_q), .b(B_q), .out(adder_1_out));  // open: cin, cout
endmodule
