// Logisim project fib_auto .circ as structural Verilog: 1 circuit, main circuit main
module main (
  input  in_1
);

  wire and_1_out, and_2_out, and_3_out, and_4_out, button_1_out, clock_1_out, controlled_buffer_1_out,
       controlled_buffer_2_out, controlled_buffer_3_out, controlled_buffer_4_out, controlled_buffer_5_out,
       controlled_buffer_7_out, counter_2_q, demultiplexer_1_out0, demultiplexer_1_out1,
       demultiplexer_1_out2, demultiplexer_2_out0, demultiplexer_2_out1, not_1_out, not_2_out, not_3_out,
       not_4_out, s_r_ff_1_q, s_r_ff_2_q, s_r_ff_3_q, s_r_ff_3_qn;
  wire [1:0] counter_1_q;
  wire [31:0] A_q, adder_1_out, B_q, C_q, controlled_buffer_8_out;

  Clock clock_1 (.out(clock_1_out));
  Button button_1 (.out(button_1_out));
  and and_1 (and_1_out, clock_1_out, in_1);
  S_R_Flip_Flop s_r_ff_1 (.Q(s_r_ff_1_q), .preset(button_1_out), .reset(and_4_out));  // open: S, clk, R, Qn, en
  and and_2 (and_2_out, and_1_out, s_r_ff_1_q);
  not not_1 (not_1_out, and_2_out);
  and and_3 (and_3_out, and_1_out, s_r_ff_2_q);
  S_R_Flip_Flop s_r_ff_2 (.Q(s_r_ff_2_q), .preset(and_4_out), .reset(button_1_out));  // open: S, clk, R, Qn, en
  not not_2 (not_2_out, and_3_out);
  Demultiplexer #(.select(2)) demultiplexer_1 (
    .out0(demultiplexer_1_out0), .out1(demultiplexer_1_out1), .out2(demultiplexer_1_out2), .in(and_2_out),
    .sel(counter_1_q));  // open: out3, en
  Counter #(.width(2), .max('h3)) counter_1 (
    .Q(counter_1_q), .clk(not_1_out), .clr(button_1_out));  // open: load, D, count, carry
  and and_4 (and_4_out, not_3_out, not_4_out);
  Demultiplexer demultiplexer_2 (
    .out0(demultiplexer_2_out0), .out1(demultiplexer_2_out1), .in(and_3_out), .sel(counter_2_q));  // open: en
  Counter #(.width(1), .max('h1)) counter_2 (
    .Q(counter_2_q), .clk(not_2_out), .clr(button_1_out));  // open: load, D, count, carry
  not not_3 (not_3_out, demultiplexer_1_out2);
  not not_4 (not_4_out, not_3_out);
  assign controlled_buffer_1_out = demultiplexer_1_out0 ? demultiplexer_1_out0 : 1'bz;  // Controlled_Buffer controlled_buffer_1
  assign controlled_buffer_2_out = demultiplexer_1_out0 ? demultiplexer_1_out0 : 1'bz;  // Controlled_Buffer controlled_buffer_2
  assign controlled_buffer_3_out = demultiplexer_1_out1 ? demultiplexer_1_out1 : 1'bz;  // Controlled_Buffer controlled_buffer_3
  assign controlled_buffer_4_out = demultiplexer_1_out2 ? demultiplexer_1_out2 : 1'bz;  // Controlled_Buffer controlled_buffer_4
  assign controlled_buffer_5_out = demultiplexer_2_out0 ? demultiplexer_2_out0 : 1'bz;  // Controlled_Buffer controlled_buffer_5
  assign controlled_buffer_3_out = demultiplexer_2_out1 ? demultiplexer_2_out1 : 1'bz;  // Controlled_Buffer controlled_buffer_6
  assign controlled_buffer_7_out = demultiplexer_2_out1 ? demultiplexer_2_out1 : 1'bz;  // Controlled_Buffer controlled_buffer_7
  Pull_Resistor pull_resistor_1 (.node(controlled_buffer_2_out));
  Pull_Resistor pull_resistor_2 (.node(controlled_buffer_5_out));
  Pull_Resistor pull_resistor_3 (.node(controlled_buffer_4_out));
  Pull_Resistor pull_resistor_4 (.node(controlled_buffer_7_out));
  Pull_Resistor pull_resistor_5 (.node(controlled_buffer_1_out));
  Pull_Resistor pull_resistor_6 (.node(controlled_buffer_3_out));
  S_R_Flip_Flop s_r_ff_3 (
    .Q(s_r_ff_3_q), .Qn(s_r_ff_3_qn), .preset(controlled_buffer_4_out), .reset(controlled_buffer_2_out));  // open: S, clk, R, en
  assign controlled_buffer_8_out = s_r_ff_3_qn ? 32'h1 : 32'bz;  // Controlled_Buffer controlled_buffer_8
  assign controlled_buffer_8_out = s_r_ff_3_q ? C_q : 32'bz;  // Controlled_Buffer controlled_buffer_9
  // Probe on A_q
  Register #(.width(32)) A (
    .D(B_q), .Q(A_q), .clk(controlled_buffer_7_out), .clr(controlled_buffer_1_out));  // open: en
  Register #(.width(32)) B (.D(controlled_buffer_8_out), .Q(B_q), .clk(controlled_buffer_3_out));  // open: en, clr
  Register #(.width(32)) C (.D(adder_1_out), .Q(C_q), .clk(controlled_buffer_5_out));  // open: en, clr
  Adder #(.width(32)) adder_1 (.a(A_q), .b(B_q), .out(adder_1_out));  // open: cin, cout
endmodule
